# Fritzing sketch DisplaySchalterSchaltplan (saved by Fritzing 0.9.3b)
breadboards: 1

parts:
  Bauteil1 = 1.27 inch 16-bit Color OLED w microSD holder [part_number=1673]
  Bauteil2 = Arduino Mega 2560 (Rev3)
  BUTTON1 = Arcade Button (white)
  BUTTON2 = Arcade Button (white)
  BUTTON3 = Arcade Button (white)
  BUTTON4 = Arcade Button (white)

nets:
  N1: Bauteil1.MOSI, Bauteil2.5V
  N2: Bauteil1.CLK, Bauteil2.GND, BUTTON1.no_name_yet#2, BUTTON2.no_name_yet#2, BUTTON3.no_name_yet#2, BUTTON4.no_name_yet#2
  N3: Bauteil1.DC, Bauteil2.D10_PWM
  N4: Bauteil1.RESET, Bauteil2.D8_PWM
  N5: Bauteil1.OLEDCS, Bauteil2.D9_PWM
  N6: Bauteil1.SDCS, Bauteil2.D51
  N7: Bauteil1.MISO, Bauteil2.D52
  N8: Bauteil1.SD_CD, Bauteil2.3V3
  N9: Bauteil2.D2_PWM, BUTTON2.no_name_yet#1
  N10: Bauteil2.D3_PWM, BUTTON3.no_name_yet#1
  N11: Bauteil2.D4_PWM, BUTTON4.no_name_yet#1
  N12: Bauteil2.D5_PWM, BUTTON1.no_name_yet#1

custom parts:
  1.27 inch 16-bit Color OLED w microSD holder: Our 1.27" color OLED displays are perfect when you need a small display with vivid, high-contrast 16-bit color. The visible portion of the OLED measures 1.27" diagonal and contains 128x96 RGB pixels, each one made of red, green and blue OLEDs. Each pixel can be set with 16-bits of resolution for a large range of colors. Because the display uses OLEDs, there is no backlight, and the contrast is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
  Arcade Button (white): Adafruit Arcade Button (white)
